// Logisim project cpu.circ as structural Verilog: 2 circuits, main circuit main
module main (
);

  wire clock_1_out, dipswitch_1_sw7, dipswitch_1_sw8;
  wire [7:0] counter_1_q, instruction_spliter_1_out_address, instruction_spliter_1_out_data_h,
       instruction_spliter_1_out_data_l;
  wire [15:0] instruction_spliter_1_out_data, instruction_spliter_1_out_instruction;
  wire [39:0] rom_1_data;

  ROM #(.dataWidth(40)) rom_1 (.addr(counter_1_q), .data(rom_1_data));
  DipSwitch dipswitch_1 (.sw7(dipswitch_1_sw7), .sw8(dipswitch_1_sw8));  // open: sw1, sw2, sw3, sw4, sw5, sw6
  Counter counter_1 (
    .clr(dipswitch_1_sw7), .up(1'b1), .count(dipswitch_1_sw8), .clk(clock_1_out), .Q(counter_1_q));  // open: load, D, carry
  Clock clock_1 (.out(clock_1_out));
  Instruction_Spliter instruction_spliter_1 (
    .Input_Data(rom_1_data), .Out_Data(instruction_spliter_1_out_data),
    .Out_Data_H(instruction_spliter_1_out_data_h), .Out_Data_L(instruction_spliter_1_out_data_l),
    .Out_Address(instruction_spliter_1_out_address), .Out_Instruction(instruction_spliter_1_out_instruction));
  // Probe on instruction_spliter_1_out_data
  // Probe on instruction_spliter_1_out_data_h
  // Probe on instruction_spliter_1_out_address
  // Probe on instruction_spliter_1_out_data_l

  // Notes on the sheet:
  //   contents of rom_1 (hex, n*v repeats v):
  //   33000004 10041 20065 42010002 fffeffffff
endmodule

module Instruction_Spliter (
  input  [39:0] Input_Data,
  output [15:0] Out_Data,
  output [7:0] Out_Data_H,
  output [7:0] Out_Data_L,
  output [7:0] Out_Address,
  output [15:0] Out_Instruction
);


  assign Out_Address = Input_Data[23:16];
  assign Out_Data = Input_Data[15:0];
  assign Out_Data_H = Input_Data[7:0];
  assign Out_Data_L = Input_Data[15:8];
  assign Out_Instruction = Input_Data[39:24];
endmodule
